# Fritzing sketch ArduinoMini_Photogate_Transmitter (saved by Fritzing 0.9.3b)
circuit board: 3.52994cm x 5.37276cm
breadboards: 1

parts:
  Part1 = Arduino Nano (Rev3.0)
  tranceiver = NRF24L01+ Breakout Board
  PowerSwitch = Toggle Switch [package=THT]
  Battery = Battery block 9V
  IRSensor = Infrared Proximity Sensor

nets:
  GND: Part1.GND, tranceiver.GND, Battery.-, IRSensor.GND
  N1: Part1.D9, tranceiver.CE
  N2: Part1.D10, tranceiver.CS
  N3: Part1.D11/MOSI, tranceiver.MOSI
  N4: Part1.D12/MISO, tranceiver.MISO
  N5: Part1.VIN, PowerSwitch.COM
  5V: Part1.5V, IRSensor.Vcc
  N6: Part1.A6, IRSensor.Vout
  3V3: Part1.3V3, tranceiver.VCC
  N7: Part1.D13/SCK, tranceiver.SCK
  N8: PowerSwitch.L1, Battery.+
